# Fritzing sketch fig_02-01 (saved by Fritzing 0.9.3b)
breadboards: 1

parts:
  Part1 = Arduino Uno (Rev3)
  J1 = Infrared Proximity Sensor
  C1 = Electrolytic Capacitor [capacitance=100µF package="100 mil [THT, electrolytic]"]

nets:
  N1: Part1.A0, J1.Vout
  5V: Part1.5V, J1.Vcc, C1.+
  GND: Part1.GND, J1.GND, C1.-
