# Fritzing sketch fig_04-01 (saved by Fritzing 0.9.3b)
breadboards: 1

parts:
  Part1 = Arduino Uno (Rev3)
  R1 = Resistor [tolerance=±5% resistance=1M package=THT]
  LED1 = LED - 5mm [color="Red (633nm)" package="5 mm [THT]"]
  R2 = Resistor [tolerance=±5% resistance=330 package=THT]
  J1 = Piezo Speaker
  D1 = Zener Diode [part_number=1N4732A breakdown_voltage=5.1V package="300 mil [THT]"]

nets:
  N1: Part1.A0, R1.Pin_0, J1.pin2, D1.cathode
  N2: Part1.D13/SCK, R2.Pin_0
  GND: Part1.GND, R1.Pin_1, LED1.cathode, J1.pin1, D1.anode
  N3: LED1.anode, R2.Pin_1
