# Fritzing sketch fig_05-01 (saved by Fritzing 0.9.3b)
breadboards: 1

parts:
  Part1 = Arduino Uno (Rev3)
  R2 = Resistor [tolerance=±5% resistance=10k package=THT]
  LED1 = LED - 5mm [color="Red (633nm)" package="5 mm [THT]"]
  R3 = Resistor [tolerance=±5% resistance=330 package=THT]
  R1 = SoftPot Membrane Potentiometer [package=THT]

nets:
  N1: Part1.A0, R2.Pin_1, R1.wiper
  N2: Part1.D13/SCK, R3.Pin_0
  GND: Part1.GND, R2.Pin_0, LED1.cathode, R1.leg1
  5V: Part1.5V, R1.leg2
  N3: LED1.anode, R3.Pin_1

custom parts:
  SoftPot Membrane Potentiometer: A thin variable potentiometer. Based on the potentiometer part by f.althaus.
