# Fritzing sketch fig_07-01 (saved by Fritzing 0.9.3b)
breadboards: 1

parts:
  Part1 = Arduino Uno (Rev3)
  R2 = Resistor [tolerance=±5% resistance=10k package=THT]
  R1 = Basic Flex Resistor

nets:
  N1: Part1.A0, R2.Pin_0, R1.pin_1
  5V: Part1.5V, R1.Pin_2
  GND: Part1.GND, R2.Pin_1
