# Fritzing sketch fig_11-01 (saved by Fritzing 0.9.3b)
breadboards: 1

parts:
  Part1 = Arduino Uno (Rev3)
  M2 = AE-HMC5883L [package="DIP (Dual Inline) [THT]"]
  M1 = AE-PCA9306 [package="DIP (Dual Inline) [THT]"]
  LED1 = RGB LED (com. cathode, rbg) [package="5 mm [THT]"]
  R1 = Resistor [tolerance=±5% resistance=150 package=THT]
  R2 = Resistor [tolerance=±5% resistance=150 package=THT]
  R3 = Resistor [tolerance=±5% resistance=330 package=THT]

nets:
  N1: Part1.A4/SDA, M1.SDA2
  N2: Part1.A5/SCL, M1.SCL2
  N3: Part1.D9_PWM, R3.Pin_1
  N4: Part1.D10_PWM/SS, R2.Pin_1
  N5: Part1.D11_PWM/MOSI, R1.Pin_1
  3.3V: Part1.3V3, M2.VDD, M1.VREF1
  5V: Part1.5V, M1.VREF2
  GND: Part1.GND, M2.GND, M1.GND, LED1.common_cathode
  N6: M2.SDA, M1.SDA1
  N7: M2.SCL, M1.SCL1
  N8: LED1.red_anode, R3.Pin_0
  N9: LED1.blue_anode, R2.Pin_0
  N10: LED1.green_anode, R1.Pin_0

custom parts:
  AE-HMC5883L: A HMC5883L breakout board by Akizuki Denshi Tsusho Co.,Ltd.
  AE-PCA9306: A PCA9306 breakout board by Akizuki Denshi Tsusho Co.,Ltd.
