# Fritzing sketch fig_12-01 (saved by Fritzing 0.9.3b)
breadboards: 1

parts:
  Part1 = Arduino Uno (Rev3)
  R1 = Resistor [tolerance=±5% resistance=10k package=THT]
  LED1 = LED - 5mm [color="Red (633nm)" package="5 mm [THT]"]
  R2 = Resistor [tolerance=±5% resistance=330 package=THT]
  S1 = NaPiOn

nets:
  N1: Part1.D13/SCK, R2.Pin_0
  GND: Part1.GND, R1.Pin_0, LED1.cathode, S1.GND
  N2: Part1.D2, R1.Pin_1, S1.Output
  5V: Part1.5V, S1.Vdd
  N3: LED1.anode, R2.Pin_1

custom parts:
  NaPiOn: PIR motion sensor
