# Fritzing sketch fig_13-02 (saved by Fritzing 0.9.3b)
breadboards: 1

parts:
  Part1 = Arduino Uno (Rev3)
  R1 = Resistor [tolerance=±5% resistance=1M package=THT]
  T1 = Foil [package=THT]

nets:
  N1: Part1.D2, R1.Pin_1
  N2: Part1.D3_PWM, R1.Pin_0, T1.Terminal
