# Fritzing sketch fig_15-02 (saved by Fritzing 0.9.3b)
breadboards: 1

parts:
  Part1 = Arduino Uno (Rev3)
  LED1 = RGB LED (com. cathode, rgb) [package="5 mm [THT]"]
  R4 = Resistor [tolerance=±5% resistance=150 package=THT]
  R6 = Resistor [tolerance=±5% resistance=330 package=THT]
  R5 = Resistor [tolerance=±5% resistance=150 package=THT]
  R3 = Rotary Potentiometer (Large) [maximum_resistance=100kΩ package=THT]
  R2 = Rotary Potentiometer (Large) [maximum_resistance=100kΩ package=THT]
  R1 = Rotary Potentiometer (Large) [maximum_resistance=100kΩ package=THT]

nets:
  N1: Part1.A0, R3.wiper
  N2: Part1.A1, R2.wiper
  N3: Part1.A2, R1.wiper
  N4: Part1.D9_PWM, R6.Pin_1
  N5: Part1.D10_PWM/SS, R4.Pin_1
  N6: Part1.D11_PWM/MOSI, R5.Pin_1
  GND: Part1.GND, LED1.common_cathode, R3.leg1, R2.leg1, R1.leg1
  5V: Part1.5V, R3.leg2, R2.leg2, R1.leg2
  N7: LED1.red_anode, R6.Pin_0
  N8: LED1.green_anode, R5.Pin_0
  N9: LED1.blue_anode, R4.Pin_0
