# Fritzing sketch fig_15-05 (saved by Fritzing 0.9.3b)

parts:
  Part1 = Arduino Uno (Rev3)
  neopixel1 = Neopixel Ring 16

nets:
  GND: Part1.GND, neopixel1.GND
  N1: Part1.D2, neopixel1.IN
  5V: Part1.5V, neopixel1.VCC

custom parts:
  Neopixel Ring 16: Neopixel Ring x16
