# Fritzing sketch fig_16-02 (saved by Fritzing 0.9.3b)
breadboards: 1

parts:
  Part1 = Arduino Uno (Rev3)
  R1 = Rotary Potentiometer (Large) [maximum_resistance=10kΩ package=THT]
  L1 = Solenoid
  IC1 = Darlington Driver [package=dil18]

nets:
  N1: Part1.A0, R1.wiper
  N2: Part1.D9_PWM, IC1.1
  GND: Part1.GND, R1.leg1, IC1.9
  5V: Part1.5V, R1.leg2
  12V: Part1.VIN, L1.pin2, IC1.10
  N3: L1.pin1, IC1.18
