# Fritzing sketch fig_17-02 (saved by Fritzing 0.9.3b)
breadboards: 1

parts:
  Part1 = Arduino Uno (Rev3)
  Q1 = NPN-Transistor [package="TO92 [THT]"]
  R1 = Resistor [tolerance=±5% resistance=2.2k package=THT]
  D1 = Rectifier Diode [part_number=1N4001 package="300 mil [THT]"]
  VCC1 = Battery
  U1 = Vibration Motor- ROB-08449 [package=vibe-motor-10mm]

nets:
  N1: Part1.D9_PWM, R1.Pin_0
  GND: Part1.GND, Q1.E, VCC1.-
  N2: Q1.B, R1.Pin_1
  N3: Q1.C, D1.anode, U1.+
  N4: D1.cathode, VCC1.+, U1.-
