# Fritzing sketch fig_18-01 (saved by Fritzing 0.9.3b)
breadboards: 1

parts:
  Part1 = Arduino Uno (Rev3)
  J1 = Basic Servo
  R1 = Rotary Potentiometer (Large) [maximum_resistance=10kΩ package=THT]

nets:
  N1: Part1.A0, R1.wiper
  N2: Part1.D9_PWM, J1.pulse
  GND: Part1.GND, J1.gnd, R1.leg1
  5V: Part1.5V, J1.vcc, R1.leg2
