# Fritzing sketch fig_19-05 (saved by Fritzing 0.9.3b)
breadboards: 1

parts:
  Part1 = Arduino Uno (Rev3)
  R1 = Resistor [tolerance=±5% resistance=10k package=THT]
  M1 = DC Motor
  Part2 = Pololu TB6612FNG Dual Motor Driver Carrier

nets:
  N1: Part1.D9_PWM, Part2.AIN1
  N2: Part1.D10_PWM/SS, Part2.AIN2
  N3: Part1.D11_PWM/MOSI, Part2.PWMA
  GND: Part1.GND, Part2.GND
  5V: Part1.5V, R1.Pin_0, Part2.VCC
  12V: Part1.VIN, Part2.VM
  N4: R1.Pin_1, Part2.STBY
  N5: M1.pin_1, Part2.A01
  N6: M1.pin_2, Part2.A02

custom parts:
  Pololu TB6612FNG Dual Motor Driver Carrier: Based on the TB6612FNG breakout board by SparkFun Electronics and Fritzing
