# Fritzing sketch fig_20-02 (saved by Fritzing 0.9.3b)
breadboards: 3

parts:
  Part1 = Arduino Uno (Rev3)
  R5 = Resistor [tolerance=±5% resistance=10k package=THT]
  M1 = DC Motor
  Part2 = Pololu TB6612FNG Dual Motor Driver Carrier
  IC1 = EE-SX198 [chip_label=IC package="DIP (Dual Inline) [THT]"]
  IC2 = EE-SX198 [chip_label=IC package="DIP (Dual Inline) [THT]"]
  R1 = Resistor [tolerance=±5% resistance=150 package=THT]
  R3 = Resistor [tolerance=±5% resistance=150 package=THT]
  R2 = Resistor [tolerance=±5% resistance=10k package=THT]
  R4 = Resistor [tolerance=±5% resistance=10k package=THT]

nets:
  N1: Part1.A0, IC1.C, R2.Pin_1
  N2: Part1.A1, IC2.C, R4.Pin_1
  N3: Part1.D9_PWM, Part2.AIN1
  N4: Part1.D10_PWM/SS, Part2.AIN2
  N5: Part1.D11_PWM/MOSI, Part2.PWMA
  GND: Part1.GND, Part2.GND, IC1.A, IC2.A, R2.Pin_0, R4.Pin_0
  5V: Part1.5V, R5.Pin_0, Part2.VCC, IC1.E, IC2.E, R1.Pin_0, R3.Pin_0
  12V: Part1.VIN, Part2.VM
  N6: R5.Pin_1, Part2.STBY
  N7: M1.pin_1, Part2.A01
  N8: M1.pin_2, Part2.A02
  N9: IC1.K, R1.Pin_1
  N10: IC2.K, R3.Pin_1

custom parts:
  Pololu TB6612FNG Dual Motor Driver Carrier: Based on the TB6612FNG breakout board by SparkFun Electronics and Fritzing
  EE-SX198: A DIP stand-in part for whatever IC you want. With 4 pins on a 300mil dual inline package (DIP) footprint.
