# Fritzing sketch fig_21-02 (saved by Fritzing 0.9.3b)
breadboards: 1

parts:
  Part1 = Arduino Uno (Rev3)
  U1 = TFT [chip_label=IC package="SIP (Single Inline) [THT]"]
  S1 = Pushbutton [package="[THT]"]

nets:
  N1: Part1.D8, U1.RESET
  N2: Part1.D9_PWM, U1.D/C
  N3: Part1.D10_PWM/SS, U1.LCD_CS
  N4: Part1.D11_PWM/MOSI, U1.MOSI
  N5: Part1.D12/MISO, U1.MISO
  N6: Part1.D13/SCK, U1.SCK
  N7: Part1.D2, S1.Pin_3, S1.Pin_4
  N8: Part1.D4, U1.SD_CS
  5V: Part1.5V, U1.5V, U1.BL
  GND: Part1.GND, U1.GND, S1.Pin_1, S1.Pin_2
