# Fritzing sketch fig_23-02 (saved by Fritzing 0.9.3b)
breadboards: 1

parts:
  Part1 = Arduino Uno (Rev3)
  R1 = Resistor [tolerance=±5% resistance=10k package=THT]
  U1 = LM386 [package=dip08]
  R2 = Trimpot [package=trim_pot_pth]
  C2 = Electrolytic Capacitor [capacitance=0.22mF package="100 mil [THT, electrolytic]"]
  C1 = Ceramic Capacitor [capacitance=47pF package="200 mil [THT, multilayer]"]
  S1 = Pushbutton [package="[THT]"]
  J1 = Piezo Speaker
  R3 = Resistor [tolerance=±5% resistance=10 package=THT]

nets:
  N1: Part1.D8, R1.Pin_0, S1.Pin_3, S1.Pin_4
  N2: Part1.D11_PWM/MOSI, R2.CCW
  5V: Part1.5V, U1.V+, S1.Pin_1, S1.Pin_2
  GND: Part1.GND, R1.Pin_1, U1.-IN, U1.V-, R2.CW, J1.pin1, R3.Pin_1
  N3: U1.+IN, R2.WIPER
  N4: U1.OUT, C2.+, C1.1
  N5: C2.-, J1.pin2
  N6: C1.0, R3.Pin_0

custom parts:
  Trimpot: Small potentiometers such as Bourns's
