# Fritzing sketch fig_29-02 (saved by Fritzing 0.9.3b)
breadboards: 1

parts:
  Part1 = Arduino Uno (Rev3)
  S4 = Pushbutton [package="[THT]"]
  S3 = Pushbutton [package="[THT]"]
  S2 = Pushbutton [package="[THT]"]
  S1 = Pushbutton [package="[THT]"]
  R6 = Resistor [tolerance=±5% resistance=10k package=THT]
  R4 = Resistor [tolerance=±5% resistance=10k package=THT]
  R5 = Resistor [tolerance=±5% resistance=10k package=THT]
  R3 = Resistor [tolerance=±5% resistance=10k package=THT]
  R2 = Resistor [tolerance=±5% resistance=10k package=THT]
  R1 = Basic Force Sensing Resistor (FSR) [package=THT]

nets:
  N1: Part1.A0, R2.Pin_0, R1.pin_0
  N2: Part1.D2, S4.Pin_3, S4.Pin_4, R6.Pin_0
  N3: Part1.D3_PWM, S3.Pin_3, S3.Pin_4, R5.Pin_0
  N4: Part1.D4, S2.Pin_3, S2.Pin_4, R4.Pin_0
  N5: Part1.D5_PWM, S1.Pin_3, S1.Pin_4, R3.Pin_0
  5V: Part1.5V, S4.Pin_1, S4.Pin_2, S3.Pin_1, S3.Pin_2, S2.Pin_1, S2.Pin_2, S1.Pin_1, S1.Pin_2, R1.pin_1
  GND: Part1.GND, R6.Pin_1, R4.Pin_1, R5.Pin_1, R3.Pin_1, R2.Pin_1

custom parts:
  Pushbutton: A generic pushbutton.
