# Fritzing sketch fig_30-02 (saved by Fritzing 0.9.3b)
breadboards: 1

parts:
  Part1 = Arduino Uno (Rev3)
  IC1 = DIP - 8 pins [chip_label=IC package="DIP (Dual Inline) [THT]"]
  S1 = Pushbutton [package="[THT]"]
  R1 = Resistor [tolerance=±5% resistance=10k package=THT]

nets:
  N1: Part1.A0, IC1.Out_X
  N2: Part1.A1, IC1.Out_Y
  N3: Part1.A2, IC1.Out_Z
  N4: Part1.D2, S1.Pin_3, S1.Pin_4, R1.Pin_0
  5V: Part1.5V, IC1.Vdd, IC1.Enable, S1.Pin_1, S1.Pin_2
  GND: Part1.GND, IC1.GND, IC1.Self_test, R1.Pin_1

custom parts:
  DIP - 8 pins: A DIP stand-in part for whatever IC you want. With 8 pins on a 300mil dual inline package (DIP) footprint.
