# Fritzing sketch fig_31-02 (saved by Fritzing 0.9.3b)
breadboards: 1

parts:
  Part1 = Arduino Uno (Rev3)
  LED1 = LED - 5mm [color="Red (633nm)" package="5 mm [THT]"]
  R1 = Resistor [tolerance=±5% resistance=330 package=THT]
  R3 = Resistor [tolerance=±5% resistance=10k package=THT]
  S1 = Pushbutton [package="[THT]"]
  S2 = Pushbutton [package="[THT]"]
  R2 = Resistor [tolerance=±5% resistance=10k package=THT]

nets:
  N1: Part1.D8, S2.Pin_3, S2.Pin_4, R2.Pin_0
  N2: Part1.D9_PWM, R3.Pin_0, S1.Pin_3, S1.Pin_4
  N3: Part1.D13/SCK, R1.Pin_0
  GND: Part1.GND, LED1.cathode, R3.Pin_1, R2.Pin_1
  5V: Part1.5V, S1.Pin_1, S1.Pin_2, S2.Pin_1, S2.Pin_2
  N4: LED1.anode, R1.Pin_1
