# Fritzing sketch fig_32-04 (saved by Fritzing 0.9.3b)
breadboards: 1

parts:
  Part1 = Adafruit Feather 32u4 Bluefruit [part_number="Adafruit #2829"]
  S1 = Pushbutton [package="[THT]"]
  R1 = Resistor [tolerance=±5% resistance=10k package=THT]

nets:
  GND: Part1.GND, R1.Pin_1
  3.3V: Part1.+3V3, S1.Pin_1, S1.Pin_2
  N1: Part1.2, S1.Pin_3, S1.Pin_4, R1.Pin_0

custom parts:
  Adafruit Feather 32u4 Bluefruit: This is the Adafruit Feather 32u4 Bluefruit - our take on an 'all-in-one' Arduino-compatible + Bluetooth Low Energy with built in USB and battery charging. Its an Adafruit Feather 32u4 with a BTLE module, ready to rock! We have other boards in the Feather family, check'em out here. Bluetooth Low Energy is the hottest new low-power, 2.4GHz spectrum wireless protocol. In particular, its the only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
