# Fritzing sketch fig_32-11 (saved by Fritzing 0.9.3b)
breadboards: 1

parts:
  Part1 = Adafruit Feather 32u4 Bluefruit [part_number="Adafruit #2829"]
  Part2 = Adafruit MPR121
  T1 = Foil [package=THT]
  T2 = Foil [package=THT]
  T3 = Foil [package=THT]
  T4 = Foil [package=THT]

nets:
  GND: Part1.GND, Part2.GND
  3.3V: Part1.+3V3, Part2.VIN
  N1: Part1.3, Part2.SCL
  N2: Part1.2, Part2.SDA
  N3: Part2.ELEC3, T4.Terminal
  N4: Part2.ELEC2, T3.Terminal
  N5: Part2.ELEC1, T2.Terminal
  N6: Part2.ELEC0, T1.Terminal

custom parts:
  Adafruit Feather 32u4 Bluefruit: This is the Adafruit Feather 32u4 Bluefruit - our take on an 'all-in-one' Arduino-compatible + Bluetooth Low Energy with built in USB and battery charging. Its an Adafruit Feather 32u4 with a BTLE module, ready to rock! We have other boards in the Feather family, check'em out here. Bluetooth Low Energy is the hottest new low-power, 2.4GHz spectrum wireless protocol. In particular, its the only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
  Adafruit MPR121: Add lots of touch sensors to your next microcontroller project with this easy-to-use 12-channel capacitive touch sensor breakout board, starring the MPR121. This chip can handle up to 12 individual touch pads. The MPR121 has support for only I2C, which can be implemented with nearly any microcontroller. You can select one of 4 addresses with the ADDR pin, for a total of 48 capacitive touch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
