# Fritzing sketch fig_32-14 (saved by Fritzing 0.9.3b)
breadboards: 1

parts:
  Part1 = Adafruit Feather 32u4 Bluefruit [part_number="Adafruit #2829"]
  U1 = SIP - 3 pins [chip_label=IC package="SIP (Single Inline) [THT]"]

nets:
  N1: Part1.A0, U1.Vout
  GND: Part1.GND, U1.GND
  +3V3: Part1.+3V3, U1.VCC

custom parts:
  Adafruit Feather 32u4 Bluefruit: This is the Adafruit Feather 32u4 Bluefruit - our take on an 'all-in-one' Arduino-compatible + Bluetooth Low Energy with built in USB and battery charging. Its an Adafruit Feather 32u4 with a BTLE module, ready to rock! We have other boards in the Feather family, check'em out here. Bluetooth Low Energy is the hottest new low-power, 2.4GHz spectrum wireless protocol. In particular, its the only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
  SIP - 3 pins: A SIP stand-in part for whatever you want. With 3 pins on a 300 mil single inline package (SIP) footprint.
