# Fritzing sketch fig_33-03 (saved by Fritzing 0.9.3b)
breadboards: 1

parts:
  S1 = Pushbutton [package="[THT]"]
  R1 = Resistor [tolerance=±5% resistance=10k package=THT]
  Part1 = ESPr Developer [package="DIP (Dual Inline) [THT]"]

nets:
  3.3V: S1.Pin_1, S1.Pin_2, Part1.3V3
  N1: S1.Pin_3, S1.Pin_4, R1.Pin_0, Part1.IO12
  GND: R1.Pin_1, Part1.GND#8

custom parts:
  ESPr Developer: An ESP-WROOM-02 breakout board by Switch Science
