# Fritzing sketch fig_34-02 (saved by Fritzing 0.9.3b)
breadboards: 1

parts:
  R1 = Resistor [tolerance=±5% resistance=1k package=THT]
  LED1 = LED - 5mm [color="Red (633nm)" package="5 mm [THT]"]
  Part1 = ESPr Developer [package="DIP (Dual Inline) [THT]"]

nets:
  N1: R1.Pin_0, Part1.IO14
  N2: R1.Pin_1, LED1.anode
  GND: LED1.cathode, Part1.GND#8

custom parts:
  ESPr Developer: An ESP-WROOM-02 breakout board by Switch Science
