# Fritzing sketch fig_I_04-02 (saved by Fritzing 0.9.3b)
breadboards: 1

parts:
  Part1 = Arduino Uno (Rev3)
  LED1 = LED - 5mm [color="Red (633nm)" package="5 mm [THT]"]
  R1 = Resistor [tolerance=±5% resistance=330 package=THT]

nets:
  N1: Part1.D9_PWM, R1.Pin_0
  GND: Part1.GND, LED1.cathode
  5V: Part1.5V
  N2: LED1.anode, R1.Pin_1
