# Fritzing sketch fig_I_04-04 (saved by Fritzing 0.9.3b)
breadboards: 1

parts:
  Part1 = Arduino Uno (Rev3)
  R2 = Resistor [tolerance=±5% resistance=10k package=THT]
  LED1 = LED - 5mm [color="Red (633nm)" package="5 mm [THT]"]
  R1 = Resistor [tolerance=±5% resistance=330 package=THT]
  S1 = Pushbutton [package="[THT]"]

nets:
  N1: Part1.D13/SCK, R1.Pin_0
  N2: Part1.D2, R2.Pin_1, S1.Pin_1, S1.Pin_2
  5V: Part1.5V, R2.Pin_0
  GND: Part1.GND, LED1.cathode, S1.Pin_3, S1.Pin_4
  N3: LED1.anode, R1.Pin_1
