# Fritzing sketch fig_I_04-06 (saved by Fritzing 0.9.3b)
breadboards: 1

parts:
  Part1 = Arduino Uno (Rev3)
  LED1 = LED - 5mm [color="Red (633nm)" package="5 mm [THT]"]
  R2 = Resistor [tolerance=±5% resistance=330 package=THT]
  R1 = Rotary Potentiometer (Large) [maximum_resistance=10kΩ package=THT]

nets:
  N1: Part1.A0, R1.wiper
  N2: Part1.D9_PWM, R2.Pin_0
  5V: Part1.5V, R1.leg2
  GND: Part1.GND, LED1.cathode, R1.leg1
  N3: LED1.anode, R2.Pin_1
