# Fritzing sketch fig_I_04-10 (saved by Fritzing 0.9.3b)
circuit board: 8.46667cm x 5.64444cm
breadboards: 1

parts:
  Part1 = Arduino Uno (Rev3)
  R1 = Trimpot [package=trim_pot_pth]
  R2 = Resistor [tolerance=±5% resistance=150 package=THT]
  LCD1 = LCD screen

nets:
  N1: Part1.D11_PWM/MOSI, LCD1.E
  N2: Part1.D12/MISO, LCD1.RS
  GND: Part1.GND, R1.CW, LCD1.VSS, LCD1.R/W, LCD1.LED-
  N3: Part1.D2, LCD1.DB7
  N4: Part1.D3_PWM, LCD1.DB6
  N5: Part1.D4, LCD1.DB5
  N6: Part1.D5_PWM, LCD1.DB4
  5V: Part1.5V, R1.CCW, R2.Pin_1, LCD1.VDD
  N7: R1.WIPER, LCD1.V0
  N8: R2.Pin_0, LCD1.LED+

custom parts:
  Trimpot: Small potentiometers such as Bourns's
  LCD screen: SD1602VBWB-XA
